# Fritzing sketch electrical-sketch (saved by Fritzing 0.9.6b)
perfboards: 1

parts:
  M1 = MKR ZERO
  U1 = MCP4725 [package=SOT23-6]
  U2 = Voltage Regulator - 5V [package="TO220 [THT]"]
  J1 = Power Jack [package=power_jack_pth]
  J2 = Camdenboss CTB0158-5 [part_number=CTB0158-5 package=THT]

nets:
  N1: M1.D0, J2.pin2
  N2: M1.D11_SDA, M1.SDA, U1.SDA
  N3: M1.D12_SCL, M1.SCL, U1.SCL
  GND: M1.GND, U1.VSS, U2.GND, J1.GND, J2.pin3, J2.pin4
  VCC: M1.VCC, U1.VDD
  N4: M1.VIN, U2.output_voltage
  N5: U1.VOUT, J2.pin5
  N6: U2.input_voltage, J1.PWR, J2.pin1

custom parts:
  MKR ZERO: arduino mrk zero SAMD21 Cortex-M0+ 32bit low power ARM MCU 256 meg flash 32kb sram 48mhz
